# Fritzing sketch Esp8266_wiring_diagram (saved by Fritzing 0.9.3b)
breadboards: 1

parts:
  L298N1 = L298N DC motor driver
  U1 = ESP8266 NodeMCU LoLin module
  U2 = LIPO-2000mAh [package=lipo-2000]
  U3 = LIPO-2000mAh [package=lipo-2000]
  M2 = DC Motor
  M1 = DC Motor
  hc-sr1 = hc-sr04
  R8 = Resistor [tolerance=±5% resistance=10k package=THT]
  R9 = Resistor [tolerance=±5% resistance=10k package=THT]

nets:
  N1: L298N1.OUT1, M2.pin_2
  N2: L298N1.OUT2, M2.pin_1
  N3: L298N1.OUT3, M1.pin_2
  N4: L298N1.OUT4, M1.pin_1
  N5: L298N1.12V, U2.+, R9.Pin_0
  GND: L298N1.GND, U1.GND, U3.-, hc-sr1.GND, R8.Pin_0, R8.Pin_1, R9.Pin_1
  VIN: L298N1.5V#7, U1.Vin, hc-sr1.VCC
  N6: L298N1.5V#9, L298N1.ENA
  N7: L298N1.5V#10, L298N1.ENB
  N8: L298N1.IN1, U1.D2
  N9: L298N1.IN2, U1.D3
  N10: L298N1.IN3, U1.D4
  N11: L298N1.IN4, U1.D5
  N12: U1.D0, U1.D1, hc-sr1.Trig, hc-sr1.Echo
  N13: U2.-, U3.+

notes:
  ADC_E
  10k

custom parts:
  L298N DC motor driver: 2x DC motor driver with 78M05 positive voltage regulator (7..35 V) L298N: max 46 V, 2 A Set 5 V Enable jumper to enable 5 V regultor (needed for the L298N) and +5 V output at screw terminal or supply external +5 V at screw terminal Set ENA and/or ENB to +5 V to enable motor permanently or supply ENA and/or ENB with PWM signal IN1 and IN2 set rotation directory for motor A (OUT1/OUT2) IN2 and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
  ESP8266 NodeMCU LoLin module: ESP8266 based NodeMCU
